# Fritzing sketch Module_Detector (saved by Fritzing 0.9.6b)
breadboards: 1

parts:
  A1 = MQ-2 breakout
  Part1 = SRF05 Ultrasonic Rangefinder
  SG1 = Buzzer 12mm [part_number=COM-07950 package=buzzer-12mm-ns]
  S1 = Pushbutton [package="[THT]"]
  LED1 = LED - 5mm [color="Red (633nm)" current=0.030 package="5 mm [THT]"]
  LED2 = LED - 5mm [color="Green (555nm)" current=0.030 package="5 mm [THT]"]
  R1 = Resistor [tolerance=±5% resistance=1k package="2010 [SMD]"]
  R2 = Resistor [tolerance=±5% resistance=1k package="2010 [SMD]"]
  M1 = DOIT Esp32 DevKit v1 (30 pins long, 11 pins width) [part_number=ESP32S-PIN30]

nets:
  VCC: A1.VCC, Part1.VCC, M1.3V3
  GND: A1.GND, Part1.GND, SG1.2, S1.Pin_1, S1.Pin_2, M1.GND
  N1: A1.AO, M1.D4
  N2: Part1.Trig, M1.D19
  N3: Part1.Echo, M1.D18
  N4: SG1.1, M1.D2
  N5: S1.Pin_3, S1.Pin_4, M1.D5
  N6: LED1.cathode, LED2.cathode, R1.Pin_1
  N7: LED1.anode, M1.D15
  N8: LED2.anode, M1.D23
  N9: R1.Pin_0, R2.Pin_1

custom parts:
  MQ-2 breakout: MQ-2 gas sensor
  Buzzer 12mm: Buzzer 12mm Spark Fun Electronics SKU : Comp-Buzzer Through hole This is a small 12mm round speaker that operates around the audible 2kHz range. You can use these speakers to create simple music or user interfaces. This is not a true piezoelectric speaker but behaves similarly. Instead of a piezoelectric crystal that vibrates with an electric current, this tiny speaker uses an electromagnet to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
  DOIT Esp32 DevKit v1 (30 pins long, 11 pins width): The DOIT Esp32 DevKit v1 is one of the development board created by DOIT to evaluate the ESP-WROOM-32 module. It is based on the ESP32 microcontroller that boasts Wifi, Bluetooth, Ethernet and Low Power support all in a single chip. (vanepp) made breadboard work, adjusted pin numbering and labels and reduced size of schematic and cleaned up pcb. This chip is 30pins long (2 x15) and 11 pins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
