# Fritzing sketch Modulo_Central (saved by Fritzing 0.9.6b)
breadboards: 1

parts:
  Buzzer = Piezo Speaker
  part = DOIT Esp32 DevKit v1 (30 pins long, 11 pins width) [part_number=ESP32]
  Button = Momentary Switch [package=ksa_sealed_tac_switch]
  part_2 = Resistor [tolerance=±5% resistance=1k power=0.25 package=THT]
  part_3 = Resistor [tolerance=±5% resistance=1k power=0.25 package=THT]
  part_4 = LED - 3mm [color="Red (633nm)" current=0.030 package="3 mm [THT]"]
  part_5 = LED - 3mm [color="Green (555nm)" current=0.030 package="3 mm [THT]"]
  Display1 = LCD screen 16x2 IIC [part_number=101290]
  DTH11_MODULE = KY-015 Temperature & Humidity Sensor Module [package="Breakout board"]

nets:
  GND: Buzzer.pin1, part.GND, Button.1, Button.2, part_2.Pin_1, Display1.GND, DTH11_MODULE.-
  N1: Buzzer.pin2, part.D2
  3V3: part.3V3, DTH11_MODULE.Vin
  N2: part.D4, DTH11_MODULE.S
  N3: part.D5, Button.3, Button.4
  N4: part.D18, part_4.cathode
  N5: part.D19, part_5.cathode
  N6: part.D21, Display1.SDA
  N7: part.D22, Display1.SCL
  VIN: part.VIN, Display1.VCC
  N8: part_2.Pin_0, part_3.Pin_1
  N9: part_3.Pin_0, part_4.anode, part_5.anode

custom parts:
  DOIT Esp32 DevKit v1 (30 pins long, 11 pins width): The DOIT Esp32 DevKit v1 is one of the development board created by DOIT to evaluate the ESP-WROOM-32 module. It is based on the ESP32 microcontroller that boasts Wifi, Bluetooth, Ethernet and Low Power support all in a single chip. (vanepp) made breadboard work, adjusted pin numbering and labels and reduced size of schematic and cleaned up pcb. This chip is 30pins long (2 x15) and 11 pins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
  LCD screen 16x2 IIC: LCD screen with HD44780 controller enables showing text, symbols, value or anything else that comes from Croduino/Arduino. It is capable of showing 16 symbols in two lines and therefore can be used in many projects that need to send clearly visible and legible output information.. • Color of symbols: White • Backlight: Blue • Dimensions: 80 x 36 x 12 mm • Screen dimensions: 64.5 x 16 mm •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
  KY-015 Temperature & Humidity Sensor Module: KY-015 temperature and humidity sensor module, provides a low-latency serial interface to measure humidity and temperature.
