# Fritzing sketch Modulo_Clima (saved by Fritzing 0.9.6b)
breadboards: 1

parts:
  M1 = DOIT Esp32 DevKit v1 (30 pins long, 11 pins width) [part_number=ESP32S-PIN30]
  LED1 = LED - 5mm [color="Red (633nm)" current=0.030 package="5 mm [THT]"]
  LED2 = LED - 5mm [color="Green (555nm)" current=0.030 package="5 mm [THT]"]
  R1 = Resistor [tolerance=±5% resistance=1k package="0603 [SMD]"]
  R2 = Resistor [tolerance=±5% resistance=1k package="0603 [SMD]"]
  IR1 = tl1838 [package=THT]
  D1 = LTE-302 [package=lte-302]
  S1 = Pushbutton [package="[THT]"]

nets:
  3V3: M1.3V3, IR1.VCC
  GND: M1.GND, R2.Pin_0, IR1.GND, D1.C, S1.Pin_1, S1.Pin_2
  N1: M1.D4, IR1.OUT
  N2: M1.D5, S1.Pin_3, S1.Pin_4
  N3: M1.D18, LED1.anode
  N4: M1.D19, LED2.anode
  N5: M1.D23, D1.A
  N6: LED1.cathode, LED2.cathode, R1.Pin_1
  N7: R1.Pin_0, R2.Pin_1

custom parts:
  DOIT Esp32 DevKit v1 (30 pins long, 11 pins width): The DOIT Esp32 DevKit v1 is one of the development board created by DOIT to evaluate the ESP-WROOM-32 module. It is based on the ESP32 microcontroller that boasts Wifi, Bluetooth, Ethernet and Low Power support all in a single chip. (vanepp) made breadboard work, adjusted pin numbering and labels and reduced size of schematic and cleaned up pcb. This chip is 30pins long (2 x15) and 11 pins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
  tl1838: The TL1838 is a miniaturized receiver for infrared remote control systems. A PIN diode and a preamplifier are assembled on a lead frame, the epoxy package acts as an IR filter. The demodulated output signal can be directly decoded by a microprocessor.
